# Fritzing sketch Origo2022_Circuit (saved by Fritzing 0.9.3b)
circuit board: 8.46667cm x 5.64444cm

parts:
  U1 = NodeMCU V1.0
  IC1 = L293D [package=THT]
  VCC1 = Battery block 9V
  VCC2 = 4 x AAA Battery Mount  # not connected
  M1 = DC Motor  # not connected
  M2 = DC Motor  # not connected

nets:
  N1: U1.D1, IC1.In_1
  N2: U1.D2, IC1.In_2, VCC1.-
  N3: U1.D3, IC1.In_3
  N4: U1.D4, IC1.In_4
  N5: U1.GND, IC1.0V
  N6: U1.D6, IC1.Enable_1
  N7: U1.D7, IC1.Enable_2
  N8: IC1.+Vmotor, IC1.+V

notes:
  Schematics

custom parts:
  NodeMCU V1.0: ESP8266 based NodeMCU
